# Fritzing sketch lars (saved by Fritzing 0.9.2b)
breadboards: 1

parts:
  Part1 = Arduino Yun
  R1 = Resistor [tolerance=±5% resistance=220 package=THT]
  J1 = Screw terminal - 2 pins [package=THT]
  J2 = Screw terminal - 2 pins [package=THT]
  T1 = LM35 Temperature Sensor [package="TO92 [THT]"]
  T2 = LM35 Temperature Sensor [package="TO92 [THT]"]
  U1 = mystery part, 4 pins [chip_label=?]

nets:
  N1: Part1.ICSP_MISO, Part1.D9_PWM, Part1.D10_PWM/SS, Part1.D11_PWM/MOSI, Part1.D12/MISO, U1.pin3
  N2: Part1.5V, R1.Pin_1, T1.+Vs, T2.+Vs
  GND: Part1.GND, J2.pin1, T1.GND, T2.GND, U1.pin4
  N3: Part1.D2, R1.Pin_0, T1.Vout, T2.Vout
  N4: Part1.VIN, J2.pin2
  N5: J1.pin1, U1.pin1
  N6: J1.pin2, U1.pin2
